# Fritzing sketch exp1 (saved by Fritzing 0.9.3b)
breadboards: 1

parts:
  Part1 = Arduino Uno (Rev3)
  LED1 = smd LED [color="Red (633nm)" package="1206 [SMD]"]
  R1 = Resistor [tolerance=±5% resistance=150 package="1206 [SMD]"]

nets:
  N1: Part1.GND, R1.Pin_0
  N2: LED1.cathode, R1.Pin_1
