# Fritzing sketch exp12 (saved by Fritzing 0.9.3b)
breadboards: 1

parts:
  Part1 = Arduino Uno (Rev3)
  R1 = Resistor [tolerance=±5% resistance=220 package=THT]
  DI1 = 7-Segment LED Display [package=THT]

nets:
  N1: Part1.D8, DI1.cathodeF
  N2: Part1.D9_PWM, DI1.cathodeG
  N3: Part1.D10_PWM/SS, DI1.cathodeDP
  N4: Part1.D11_PWM/MOSI, DI1.cathodeC
  N5: Part1.D12/MISO, DI1.cathodeD
  N6: Part1.D13/SCK, DI1.cathodeE
  N7: Part1.D6_PWM, DI1.cathodeB
  N8: Part1.D7, DI1.cathodeA
  N9: R1.Pin_0, DI1.commAnode#2
