# Fritzing sketch exp4 (saved by Fritzing 0.9.3b)
breadboards: 1

parts:
  Part1 = Arduino Uno (Rev3)
  R1 = Resistor [tolerance=±5% resistance=150 package="1206 [SMD]"]
  LED1 = smd LED [color="Red (633nm)" package="1206 [SMD]"]
  S1 = Pushbutton [package="[THT]"]
  R2 = Resistor [tolerance=±5% resistance=220 package="0603 [SMD]"]

nets:
  N1: Part1.D10_PWM/SS, S1.Pin_1, S1.Pin_2, R2.Pin_0
  N2: Part1.D13/SCK, R1.Pin_0
  N3: Part1.GND, LED1.cathode, R2.Pin_1
  N4: Part1.5V, S1.Pin_3, S1.Pin_4
  N5: R1.Pin_1, LED1.anode

notes:
  10k
  255
