# Fritzing sketch exp7 (saved by Fritzing 0.9.3b)
breadboards: 1

parts:
  Part1 = Arduino Uno (Rev3)
  R1 = Resistor [tolerance=±5% resistance=220 package="0805 [SMD]"]
  R2 = Photocell (LDR) [package=THT]
  LED1 = smd LED [color="Red (633nm)" package="0805 [SMD]"]
  R3 = Resistor [tolerance=±5% resistance=10k package="1206 [SMD]"]
  LED2 = smd LED [color="Red (633nm)" package="0805 [SMD]"]

nets:
  N1: Part1.D10_PWM/SS, LED2.anode
  N2: Part1.D11_PWM/MOSI, LED1.anode
  N3: Part1.D12/MISO, R2.pin_1, R3.Pin_0
  N4: Part1.GND, R1.Pin_1, R3.Pin_1
  N5: Part1.5V, R2.pin_0
  N6: R1.Pin_0, LED1.cathode, LED2.cathode
