# Fritzing sketch exp8 (saved by Fritzing 0.9.3b)
breadboards: 1

parts:
  Part1 = Arduino Uno (Rev3)
  R1 = Resistor [tolerance=±5% resistance=220 package="0805 [SMD]"]
  LED1 = smd LED [color="Red (633nm)" package="0805 [SMD]"]
  R3 = Resistor [tolerance=±5% resistance=10k package="1206 [SMD]"]
  LED3 = LED - 3mm [color="Infrared (940nm)" package="3 mm [THT]"]
  J1 = Piezo Speaker

nets:
  N1: Part1.A0, R3.Pin_0, LED3.cathode
  N2: Part1.D10_PWM/SS, J1.pin2
  N3: Part1.D11_PWM/MOSI, LED1.anode
  N4: Part1.GND, R1.Pin_1, R3.Pin_1, J1.pin1
  N5: Part1.5V, LED3.anode
  N6: R1.Pin_0, LED1.cathode
