# Fritzing sketch exp 2 (saved by Fritzing 0.9.3b)
breadboards: 1

parts:
  Part1 = Arduino Uno (Rev3)
  LED1 = smd LED [color="Red (633nm)" package="1206 [SMD]"]
  R1 = Resistor [tolerance=±5% resistance=150 package="1206 [SMD]"]
  LED2 = smd LED [color="Yellow (595nm)" package="1206 [SMD]"]
  LED3 = smd LED [color="Green (570nm)" package="1206 [SMD]"]

nets:
  N1: Part1.GND, R1.Pin_1
  N2: Part1.D5_PWM, LED3.anode
  N3: Part1.D6_PWM, LED2.anode
  N4: Part1.D7, LED1.anode
  N5: LED1.cathode, R1.Pin_0, LED2.cathode, LED3.cathode
