# Fritzing sketch exp 3 (saved by Fritzing 0.9.3b)
breadboards: 1

parts:
  Part1 = Arduino Uno (Rev3)
  R1 = Resistor [tolerance=±5% resistance=150 package="1206 [SMD]"]
  LED1 = smd LED [color="Red (633nm)" package="1206 [SMD]"]
  LED2 = smd LED [color="Red (633nm)" package="1206 [SMD]"]
  LED3 = smd LED [color="Red (633nm)" package="1206 [SMD]"]
  LED4 = smd LED [color="Red (633nm)" package="1206 [SMD]"]
  LED5 = smd LED [color="Red (633nm)" package="1206 [SMD]"]
  LED6 = smd LED [color="Red (633nm)" package="1206 [SMD]"]

nets:
  N1: Part1.D8, LED3.anode
  N2: Part1.D9_PWM, LED2.anode
  N3: Part1.D10_PWM/SS, LED1.anode
  N4: Part1.GND, R1.Pin_0
  N5: Part1.D5_PWM, LED6.anode
  N6: Part1.D6_PWM, LED5.anode
  N7: Part1.D7, LED4.anode
  N8: R1.Pin_1, LED1.cathode, LED2.cathode, LED3.cathode, LED4.cathode, LED5.cathode, LED6.cathode
