# Fritzing sketch exp11 (saved by Fritzing 0.9.3b)
breadboards: 1

parts:
  Part1 = Arduino Uno (Rev3)
  LED1 = LED - 5mm [color="Red (633nm)" package="5 mm [THT]"]
  R1 = Resistor [tolerance=±5% resistance=220 package=THT]
  LED2 = LED - 5mm [color="Red (633nm)" package="5 mm [THT]"]
  LED3 = LED - 5mm [color="Red (633nm)" package="5 mm [THT]"]
  LED4 = LED - 5mm [color="Red (633nm)" package="5 mm [THT]"]
  LED5 = LED - 5mm [color="Red (633nm)" package="5 mm [THT]"]
  LED6 = LED - 5mm [color="Red (633nm)" package="5 mm [THT]"]
  R2 = Trimmer Potentiometer [maximum_resistance=10kΩ package=THT]

nets:
  N1: Part1.A0, R2.wiper
  N2: Part1.GND, R1.Pin_0, R2.leg2
  N3: Part1.D2, LED6.anode
  N4: Part1.D3_PWM, LED5.anode
  N5: Part1.D4, LED4.anode
  N6: Part1.D5_PWM, LED3.anode
  N7: Part1.D6_PWM, LED2.anode
  N8: Part1.D7, LED1.anode
  N9: Part1.5V, R2.leg1
  N10: LED1.cathode, R1.Pin_1, LED2.cathode, LED3.cathode, LED4.cathode, LED5.cathode, LED6.cathode
