# Fritzing sketch exp6 (saved by Fritzing 0.9.3b)
breadboards: 1

parts:
  Part1 = Arduino Uno (Rev3)
  R1 = Resistor [tolerance=±5% resistance=220 package="0805 [SMD]"]
  LED1 = RGB LED (com. cathode, rbg) [package="5 mm [THT]"]

nets:
  N1: Part1.D9_PWM, LED1.green_anode
  N2: Part1.D10_PWM/SS, LED1.blue_anode
  N3: Part1.D11_PWM/MOSI, LED1.red_anode
  N4: Part1.GND, R1.Pin_1
  N5: R1.Pin_0, LED1.common_cathode
